# Fritzing sketch RF-Sketch (saved by Fritzing 0.9.3b)
breadboards: 1

parts:
  Raspberry_Pi_1 = Raspberry Pi 3 [part_number=RPI-3-V1.2]
  U1 = mystery part, 4 pins [chip_label=?]
  U2 = mystery part, 3 pins [chip_label=?]

nets:
  N1: Raspberry_Pi_1.GPIO17, U2.pin2
  N2: Raspberry_Pi_1.GPIO27, U1.pin2
  N3: Raspberry_Pi_1.GND, U1.pin4, U2.pin3
  N4: Raspberry_Pi_1.5V, U1.pin1, U2.pin1

notes:
  MX-FS-03V (Transmitter)
  MX-05V (Receiver)
